// Logisim project SignleCycleProcessorTeam7.circ as structural Verilog: 5 circuits, main circuit RegisterFile
module RegisterFile (
  input  [2:0] Rs1,
  input  [2:0] Rs2,
  input  [2:0] Rd,
  input  Clock,
  input  [15:0] BusW,
  input  RegWrite,
  output [15:0] BusB,
  output [15:0] BusA
);

  wire and_1_out, and_2_out, and_3_out, and_4_out, and_5_out, and_6_out, and_7_out, decoder_1_out0,
       decoder_1_out1, decoder_1_out2, decoder_1_out3, decoder_1_out4, decoder_1_out5, decoder_1_out6,
       decoder_1_out7, decoder_2_out0, r1, r2, r3, r4, r5, r6, r7;
  wire [15:0] R1_q, R2_q, R3_q, R4_q, R5_q, R6_q, R7_q;

  Decoder #(.select(3), .enable("false")) decoder_1 (
    .out0(decoder_1_out0), .out1(decoder_1_out1), .out2(decoder_1_out2), .out3(decoder_1_out3),
    .out4(decoder_1_out4), .out5(decoder_1_out5), .out6(decoder_1_out6), .out7(decoder_1_out7), .sel(Rd));
  and and_1 (and_1_out, decoder_1_out1, RegWrite);
  and and_2 (and_2_out, decoder_1_out2, RegWrite);
  and and_3 (and_3_out, decoder_1_out3, RegWrite);
  and and_4 (and_4_out, decoder_1_out4, RegWrite);
  and and_5 (and_5_out, decoder_1_out5, RegWrite);
  and and_6 (and_6_out, decoder_1_out6, RegWrite);
  and and_7 (and_7_out, decoder_1_out7, RegWrite);
  Decoder #(.select(3), .enable("false")) decoder_2 (
    .out0(decoder_2_out0), .out1(r1), .out2(r2), .out3(r3), .out4(r4), .out5(r5), .out6(r6), .out7(r7),
    .sel(Rs1));
  assign BusA = decoder_2_out0 ? {16{1'b0}} : 16'bz;  // Controlled_Buffer controlled_buffer_1
  Register #(.width(16)) u_R1 (.D(BusW), .en(and_1_out), .Q(R1_q), .clk(Clock));  // open: clr
  Register #(.width(16)) u_R2 (.D(BusW), .en(and_2_out), .Q(R2_q), .clk(Clock));  // open: clr
  Register #(.width(16)) u_R3 (.D(BusW), .en(and_3_out), .Q(R3_q), .clk(Clock));  // open: clr
  Register #(.width(16)) u_R4 (.D(BusW), .en(and_4_out), .Q(R4_q), .clk(Clock));  // open: clr
  Register #(.width(16)) u_R5 (.D(BusW), .en(and_5_out), .Q(R5_q), .clk(Clock));  // open: clr
  Register #(.width(16)) u_R6 (.D(BusW), .en(and_6_out), .Q(R6_q), .clk(Clock));  // open: clr
  Register #(.width(16)) u_R7 (.D(BusW), .en(and_7_out), .Q(R7_q), .clk(Clock));  // open: clr
  assign BusA = r1 ? R1_q : 16'bz;  // Controlled_Buffer controlled_buffer_2
  assign BusA = r2 ? R2_q : 16'bz;  // Controlled_Buffer controlled_buffer_3
  assign BusA = r3 ? R3_q : 16'bz;  // Controlled_Buffer controlled_buffer_4
  assign BusA = r4 ? R4_q : 16'bz;  // Controlled_Buffer controlled_buffer_5
  assign BusA = r5 ? R5_q : 16'bz;  // Controlled_Buffer controlled_buffer_6
  assign BusA = r6 ? R6_q : 16'bz;  // Controlled_Buffer controlled_buffer_7
  assign BusA = r7 ? R7_q : 16'bz;  // Controlled_Buffer controlled_buffer_8
  Multiplexer #(.select(3), .width(16), .enable("false")) multiplexer_1 (
    .in0({16{1'b0}}), .in1(R1_q), .in2(R2_q), .in3(R3_q), .in4(R4_q), .in5(R5_q), .in6(R6_q), .in7(R7_q),
    .out(BusB), .sel(Rs2));

  // Notes on the sheet:
  //   Register File
endmodule

module ALU (
  input  [15:0] A,
  input  [15:0] B,
  input  [3:0] ALUop,
  output [15:0] BusA
);

  wire comparator_1_lt, comparator_2_lt;
  wire [15:0] add, \and , \or , sll, slt, sltu, sra, srl, sub, \xor ;

  Adder #(.width(16)) adder_1 (.a(A), .b(B), .out(add));  // open: cin, cout
  Subtractor #(.width(16)) subtractor_1 (.a(A), .b(B), .out(sub));  // open: bin, bout
  Shifter #(.width(16)) shifter_1 (.in(A), .\dist (B[3:0]), .out(sll));
  Shifter #(.width(16), .shift("ar")) shifter_2 (.in(A), .\dist (B[3:0]), .out(sra));
  Shifter #(.width(16), .shift("lr")) shifter_3 (.in(A), .\dist (B[3:0]), .out(srl));
  Comparator #(.width(16), .mode("unsigned")) comparator_1 (.a(A), .b(B), .lt(comparator_1_lt));  // open: gt, eq
  assign sltu = {{15{1'b0}}, comparator_1_lt};  // Bit_Extender bit_extender_1
  assign slt = {{15{1'b0}}, comparator_2_lt};  // Bit_Extender bit_extender_2
  Comparator #(.width(16)) comparator_2 (.a(A), .b(B), .lt(comparator_2_lt));  // open: gt, eq
  assign \xor  = A ^ B;  // XOR_Gate xor_1, 16 bits wide
  assign \or  = A | B;  // OR_Gate or_1, 16 bits wide
  assign \and  = A & B;  // AND_Gate and_1, 16 bits wide
  Multiplexer #(.select(4), .width(16), .enable("false")) multiplexer_1 (
    .in0(add), .in1(sub), .in2(slt), .in3(sltu), .in4(\xor ), .in5(\or ), .in6(\and ), .in7(sll), .in8(srl),
    .in9(sra), .in10({B[10:0], {5{1'b0}}}), .out(BusA), .sel(ALUop));  // open: in11, in12, in13, in14, in15

  // Other names for the same wires on the sheet: lui[15:5] = B[10:0]

  // Notes on the sheet:
  //   Arithemetic and Logical Unit
endmodule

module DataPath (
);

  wire Clock, Extend, MemRead, MemWrite, RegWrite;
  wire [1:0] ALUsrc, f, RegRD, WB;
  wire [2:0] imm2_3, imm5, multiplexer_3_out;
  wire [3:0] aluOP;
  wire [4:0] OpCode;
  wire [5:3] imm11;
  wire [15:0] ALUResult, bit_extender_1_out, bit_extender_2_out, bit_extender_3_out, bit_extender_4_out,
       BusSelection, multiplexer_1_out, PC, PC_1, pccontrol_1_out_9, Ra, ram_1_data, Rb, WBValue;

  PCControl pccontrol_1 (
    .Opcode(OpCode), .Rs1(Ra), .Rs2(Rb), .out_9(pccontrol_1_out_9), .PC(PC),
    .imm11({f, imm5, imm11, imm2_3}), .imm2_3({f, imm2_3}), .imm5({f, imm5}), .out_8(PC_1));
  Register #(.width(16)) u_PC (.D(pccontrol_1_out_9), .en(1'b1), .Q(PC), .clk(Clock));  // open: clr
  Clock clock_1 (.out(Clock));
  ROM #(.addrWidth(16), .dataWidth(16)) rom_1 (.addr(PC), .data({f, imm5, imm11, imm2_3, OpCode}));  // open: sel
  assign bit_extender_1_out = {{11{1'b0}}, {f, imm5}};  // Bit_Extender bit_extender_1
  assign bit_extender_2_out = {{11{f[1]}}, {f, imm5}};  // Bit_Extender bit_extender_2
  assign bit_extender_3_out = {{11{f[1]}}, {f, imm2_3}};  // Bit_Extender bit_extender_3
  assign bit_extender_4_out = {{5{f[1]}}, {f, imm5, imm11, imm2_3}};  // Bit_Extender bit_extender_4
  ControlUnit controlunit_1 (
    .opCode(OpCode), .AluResult(WB), .MemRead(MemRead), .MemWrite(MemWrite), .BusB(ALUsrc), .Extend(Extend),
    .RegWrite(RegWrite), .RegDst(RegRD), .aluOP(aluOP), .f(f));
  Multiplexer #(.width(16), .enable("false")) multiplexer_1 (
    .in0(bit_extender_1_out), .in1(bit_extender_2_out), .out(multiplexer_1_out), .sel(Extend));
  Multiplexer #(.select(2), .width(16), .enable("false")) multiplexer_2 (
    .in0(Rb), .in1(multiplexer_1_out), .in2(bit_extender_3_out), .in3(bit_extender_4_out),
    .out(BusSelection), .sel(ALUsrc));
  Multiplexer #(.select(2), .width(3), .enable("false")) multiplexer_3 (
    .in0(imm2_3), .in1(3'b001), .in2(3'b111), .out(multiplexer_3_out), .sel(RegRD));  // open: in3
  RegisterFile registerfile_1 (
    .Rs1(imm11), .Rd(multiplexer_3_out), .BusB(Rb), .RegWrite(RegWrite), .BusW(WBValue), .BusA(Ra),
    .Rs2(imm5), .Clock(Clock));
  RAM #(.addrWidth(16), .dataWidth(16), .bus("separate")) ram_1 (
    .addr(ALUResult), .din(Rb), .data(ram_1_data), .str(MemWrite), .clk(Clock), .ld(MemRead));  // open: sel, clr
  ALU alu_1 (.BusA(ALUResult), .A(Ra), .B(BusSelection), .ALUop(aluOP));
  Multiplexer #(.select(2), .width(16), .enable("false")) multiplexer_4 (
    .in0(ALUResult), .in1(ram_1_data), .in2(PC_1), .out(WBValue), .sel(WB));  // open: in3

  // Other names for the same wires on the sheet: imm11 (some bits) = {f, imm5, imm2_3}; rd[2:0] = imm2_3;
  //   rs1[2:0] = imm11; rs2[2:0] = imm5; imm2_3[4:3] = f; imm5[4:3] = f

  // Notes on the sheet:
  //   Instruction Fetch
  //   contents of rom_1 (hex, n*v repeats v):
  //   7927 247 367 85a7 2ace 988 2362 a43 92a ff75
  //   BusB Selection
  //   Data Memory
endmodule

module PCControl (
  input  [4:0] Opcode,
  input  [4:0] imm5,
  input  [4:0] imm2_3,
  input  [10:0] imm11,
  input  [15:0] PC,
  input  [15:0] Rs1,
  input  [15:0] Rs2,
  output [15:0] out_8,
  output [15:0] out_9
);

  wire and_1_out, and_2_out, and_3_out, and_4_out, and_5_out, and_6_out, BEQ, BGE, BGEU, BLT, BLTU, BNE,
       comparator_1_eq, comparator_1_gt, comparator_1_lt, comparator_2_eq, comparator_2_gt, comparator_2_lt,
       J, JAL, JALR, not_1_out, or_1_out, or_2_out, or_3_out, or_4_out;
  wire [1:0] multiplexer_1_out, multiplexer_2_out, PCsrc;
  wire [15:0] adder_2_out, adder_3_out, adder_4_out, bit_extender_1_out, bit_extender_2_out,
       bit_extender_3_out, Ra;

  Decoder #(.select(5), .enable("false")) decoder_1 (
    .out14(BEQ), .out15(BNE), .out16(BLT), .out17(BGE), .out18(BLTU), .out19(BGEU), .out21(J), .out22(JAL),
    .out23(JALR), .sel(Opcode));  // open: out0, out1, out2, out3, out4, out5, out6, out7, out8, out9, out10, out11, out12, out13, out20, out24, out25, out26, out27, out28, out29, out30, out31
  Comparator #(.width(16)) comparator_1 (
    .a(Rs1), .b(Rs2), .gt(comparator_1_gt), .eq(comparator_1_eq), .lt(comparator_1_lt));
  Multiplexer #(.width(2), .enable("false")) multiplexer_1 (
    .in0(2'b00), .in1(2'b01), .out(multiplexer_1_out), .sel(or_1_out));
  or or_1 (or_1_out, J, JAL);
  not not_1 (not_1_out, comparator_1_eq);
  or or_2 (or_2_out, comparator_1_gt, comparator_1_eq);
  Multiplexer #(.width(2), .enable("false")) multiplexer_2 (
    .in0(multiplexer_1_out), .in1(2'b11), .out(multiplexer_2_out), .sel(JALR));
  and and_1 (and_1_out, BNE, not_1_out);
  and and_2 (and_2_out, or_2_out, BGE);
  and and_3 (and_3_out, comparator_1_eq, BEQ);
  and and_4 (and_4_out, comparator_1_lt, BLT);
  Multiplexer #(.width(2), .enable("false")) multiplexer_3 (
    .in0(multiplexer_2_out), .in1(2'b10), .out(PCsrc), .sel(or_3_out));
  or or_3 (or_3_out, and_3_out, and_1_out, and_4_out, and_2_out, and_6_out, and_5_out);
  and and_5 (and_5_out, or_4_out, BGEU);
  Comparator #(.width(16), .mode("unsigned")) comparator_2 (
    .a(Rs1), .b(Rs2), .gt(comparator_2_gt), .eq(comparator_2_eq), .lt(comparator_2_lt));
  and and_6 (and_6_out, comparator_2_lt, BLTU);
  or or_4 (or_4_out, comparator_2_gt, comparator_2_eq);
  assign bit_extender_1_out = {{5{imm11[10]}}, imm11};  // Bit_Extender bit_extender_1
  assign bit_extender_2_out = {{11{imm2_3[4]}}, imm2_3};  // Bit_Extender bit_extender_2
  assign bit_extender_3_out = {{11{imm5[4]}}, imm5};  // Bit_Extender bit_extender_3
  Adder #(.width(16)) adder_1 (.a(PC), .b(16'h1), .out(out_8));  // open: cin, cout
  Adder #(.width(16)) adder_2 (.a(PC), .b(bit_extender_1_out), .out(adder_2_out));  // open: cin, cout
  Adder #(.width(16)) adder_3 (.a(PC), .b(bit_extender_2_out), .out(adder_3_out));  // open: cin, cout
  Adder #(.width(16)) adder_4 (.a(Ra), .b(bit_extender_3_out), .out(adder_4_out));  // open: cin, cout
  Multiplexer #(.select(2), .width(16), .enable("false")) multiplexer_4 (
    .in0(out_8), .in1(adder_2_out), .in2(adder_3_out), .in3(adder_4_out), .out(out_9), .sel(PCsrc));

  // Other names for the same wires on the sheet: A[15:0] = Rs1; B[15:0] = Rs2

  // Notes on the sheet:
  //   PC Control Unit
  //   PCSrc Detection
  //   PC Counter
endmodule

module ControlUnit (
  input  [4:0] opCode,
  input  [1:0] f,
  output [1:0] AluResult,
  output MemRead,
  output MemWrite,
  output [1:0] BusB,
  output Extend,
  output RegWrite,
  output [1:0] RegDst,
  output [3:0] aluOP
);

  ROM #(.addrWidth(5), .dataWidth(10)) rom_1 (
    .addr(opCode), .data({RegDst, RegWrite, Extend, BusB, MemWrite, MemRead, AluResult}));  // open: sel
  ROM #(.addrWidth(7), .dataWidth(4)) rom_2 (.addr({opCode, f}), .data(aluOP));  // open: sel

  // Notes on the sheet:
  //   Main Control Unit
  //   contents of rom_1 (hex, n*v repeats v):
  //   c0 c0 c0 d0 d0 d0 6*90 d5 68 6*60 1b0 70 2f2 d2
  //   contents of rom_2 (hex, n*v repeats v):
  //   4 5 6 0 7 8 9 0 0 1 2 3 4*0 4*2 4*3 4*4 4*5 4*6 4*7 4*8 4*9 32*0 4*a
endmodule
